// Logisim project alu.circ as structural Verilog: 1 circuit, main circuit alu
module alu (
  input  [31:0] A,
  input  [31:0] B,
  input  [3:0] ALUSel,
  output [31:0] Result
);

  wire comparator_1_lt;
  wire [5:0] bitadder_1_out, bitadder_2_out;
  wire [31:0] add, and1, bit_extender_2_out, bit_extender_3_out, cnto, divu1, mulh1, mulhu1, mult1, or1,
       remu1, sll1, slll, slt1, sra1, srl1, sub1, xor1;

  Comparator #(.width(32)) comparator_1 (.a(A), .b(B), .lt(comparator_1_lt));  // open: gt, eq
  assign slt1 = {{31{1'b0}}, comparator_1_lt};  // Bit_Extender bit_extender_1
  Adder #(.width(32)) adder_1 (.a(A), .b(B), .out(add));  // open: cin, cout
  assign and1 = A & B;  // AND_Gate and_1, 32 bits wide
  assign or1 = A | B;  // OR_Gate or_1, 32 bits wide
  assign xor1 = A ^ B;  // XOR_Gate xor_1, 32 bits wide
  Shifter #(.width(32), .shift("lr")) shifter_1 (.in(A), .\dist (B[4:0]), .out(srl1));
  Shifter #(.width(32), .shift("ar")) shifter_2 (.in(A), .\dist (B[4:0]), .out(sra1));
  Shifter #(.width(32)) shifter_3 (.in(A), .\dist (B[4:0]), .out(slll));
  Divider #(.width(32)) divider_1 (.a(A), .b(B), .out(divu1));  // open: upper, rem
  Divider #(.width(32)) divider_2 (.a(A), .b(B), .rem(remu1));  // open: out, upper
  Multiplier #(.width(32)) multiplier_1 (.a(A), .b(B), .out(mult1));  // open: cin, cout
  Multiplier #(.width(32)) multiplier_2 (.a(A), .b(B), .cout(mulhu1));  // open: out, cin
  Subtractor #(.width(32)) subtractor_1 (.a(A), .b(B), .out(sub1));  // open: bin, bout
  BitAdder #(.width(32)) bitadder_1 (.in0(A), .out(bitadder_1_out));
  BitAdder #(.width(32)) bitadder_2 (.in0(B), .out(bitadder_2_out));
  assign bit_extender_2_out = {{26{1'b0}}, bitadder_1_out};  // Bit_Extender bit_extender_2
  assign bit_extender_3_out = {{26{1'b0}}, bitadder_2_out};  // Bit_Extender bit_extender_3
  Multiplexer #(.select(4), .width(32), .enable("false")) multiplexer_1 (
    .in0(add), .in1(and1), .in2(or1), .in3(xor1), .in4(srl1), .in5(sra1), .in6(sll1), .in7(slt1),
    .in8(divu1), .in9(remu1), .in10(mult1), .in11(mulhu1), .in12(sub1), .in13(cnto), .in14(mulh1),
    .out(Result), .sel(ALUSel));  // open: in15
  Adder #(.width(32)) adder_2 (.a(bit_extender_2_out), .b(bit_extender_3_out), .out(cnto));  // open: cin, cout
  xor xor_2 (mulh1[31], A[31], B[31]);
  Multiplier #(.width(31)) multiplier_3 (.a(A[30:0]), .b(B[30:0]), .cout(mulh1[30:0]));  // open: out, cin

  // Notes on the sheet:
  //   INPUTS to your circuit
  //   DON'T CHANGE THE LOCATIONS OF THE INPUTS AND OUTPUTS!
  //   OUTPUT from your circuit
endmodule
